# Fritzing sketch vent_control_ambientika (saved by Fritzing 1.0.4)
breadboards: 1

parts:
  Mod1 = Amica NodeMCU DEVKIT 1.0
  R2 = Resistor [tolerance=±5% power=0.25W resistance=10K package=THT]
  Stepdown = mystery part, 8 pins [chip_label=Stepdown]  # not connected
  Q1 = Basic FET N-Channel [package="TO220 [THT]"]
  D1 = Schottky Diode [part_number=1N5817 package="300 mil [THT]"]
  R1 = Resistor [tolerance=±5% power=0.25W resistance=10K package=THT]
  R4 = Resistor [tolerance=±5% power=0.25W resistance=10K package=THT]

nets:
  N1: Mod1.pin2, Mod1.pin_29, R2.Pin_1, Q1.source, R4.Pin_1
  N2: Mod1.pin6, Q1.gate, R4.Pin_0
  N3: Mod1.pin_30, D1.cathode, R1.Pin_1
  N4: R2.Pin_0, Q1.drain, D1.anode, R1.Pin_0

notes:
  5V
  24V
